# Fritzing sketch Schematics (saved by Fritzing 0.9.3b)
breadboards: 1

parts:
  M1 = ESP32-S2-DevKitC-1 [part_number=ESP32-S2-DevKitC-1]
  hc-sr1 = hc-sr04
  R1 = Resistor [tolerance=±5% resistance=220 package=THT]
  LED4 = LED - 3mm [color="Red (633nm)" package="3 mm [THT]"]
  LED5 = LED - 3mm [color="Red (633nm)" package="3 mm [THT]"]
  D1 = LED_BARGRAPH_10 [package=led_bargaph_10]
  R6 = Resistor [tolerance=±5% resistance=220 package=THT]
  R7 = Resistor [tolerance=±5% resistance=220 package=THT]
  R8 = Resistor [tolerance=±5% resistance=220 package=THT]
  R9 = Resistor [tolerance=±5% resistance=220 package=THT]
  R10 = Resistor [tolerance=±5% resistance=220 package=THT]
  R11 = Resistor [tolerance=±5% resistance=220 package=THT]
  R12 = Resistor [tolerance=±5% resistance=220 package=THT]
  R13 = Resistor [tolerance=±5% resistance=220 package=THT]
  R14 = Resistor [tolerance=±5% resistance=220 package=THT]
  R15 = Resistor [tolerance=±5% resistance=220 package=THT]
  S1 = Pushbutton [package="[THT]"]
  buz1 = Piezo Buzzer
  Part1 = Adafruit 2.8 inch Captouch TFT [part_number="Adafruit #2090"]

nets:
  GND: M1.pin_22, M1.pin_44, hc-sr1.GND, R1.Pin_0, R6.Pin_0, R7.Pin_0, R8.Pin_0, R9.Pin_0, R10.Pin_0, R11.Pin_0, R12.Pin_0, R13.Pin_0, R14.Pin_0, R15.Pin_0, S1.Pin_1, S1.Pin_2, buz1.pin_2, Part1.GND
  N1: M1.pin_31, S1.Pin_3, S1.Pin_4
  N2: M1.pin_32, D1.A_A
  N3: R1.Pin_1, LED4.cathode, LED5.cathode
  N4: D1.J_C, R15.Pin_1
  N5: D1.I_C, R14.Pin_1
  N6: D1.H_C, R13.Pin_1
  N7: D1.G_C, R12.Pin_1
  N8: D1.F_C, R7.Pin_1
  N9: D1.E_C, R6.Pin_1
  N10: D1.D_C, R8.Pin_1
  N11: D1.C_C, R10.Pin_1
  N12: D1.B_C, R9.Pin_1
  N13: D1.A_C, R11.Pin_1

custom parts:
  ESP32-S2-DevKitC-1: ESP32-S2-DevKitC-1 is an entry-level development board based on ESP32-S2-SOLO (on-board PCB antenna). It is based on the ESP32 microcontroller that boasts Wifi, Bluetooth, Ethernet and Low Power support all in a single chip. (vanepp) Feb 2022: converted to ESP32-S2-DevKitC-1. This module is 44pins long (2x22) and 11 pins width.
  Piezo Buzzer: Part from https://www.nutsvolts.com/magazine/article/november2012_SmileysWorkshop. Breadboard and icon images modified to be 0.3" in spacing and be more similar to the actual physical part.
  Adafruit 2.8 inch Captouch TFT: Add some jazz & pizazz to your project with a color capactive touchscreen LCD. This TFT display is big (2.8" diagonal) bright (4 white-LED backlight) and colorful! 240x320 pixels with individual RGB pixel control, this has way more resolution than a black and white 128x64 display. As a bonus, this display has a capacitive single-touch touchscreen attached to it already, so you can detect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

// code stored in the sketch: Untitled2.ino
/*  Written by Matthew Ryan Schimmel in December of 2023
  matthewschimmel.site
  Github: github.com/MatthewSchimmel/Distance-Alarm
*/
#include <Arduino_GFX_Library.h>
#define TFT_SCK    3
#define TFT_MOSI   17
#define TFT_MISO   8
#define TFT_CS     16
#define TFT_DC     15
#define TFT_RESET  7
Arduino_ESP32SPI bus = Arduino_ESP32SPI(TFT_DC, TFT_CS, TFT_SCK, TFT_MOSI, TFT_MISO);
Arduino_ILI9341 display = Arduino_ILI9341(&bus, TFT_RESET);


#define blueLight 34
#define redLight 33


//Led's for the distance indicator
#define led1 1
#define led2 2
#define led3 42
#define led4 41
#define led5 40
#define led6 39
#define led7 38
#define led8 37
#define led9 36
#define led10 35


#define echoPin 4  // attach pin D2 Arduino to pin Echo of HC-SR04
#define trigPin 5  // attach pin D3 Arduino to pin Trig of HC-SR04
//-- Wifi Segment --//
#include <WiFi.h>
#include <WiFiClient.h>
#include <WiFiAP.h>
// Set these to your desired credentials.
const char *ssid = "Nittany";
const char *password = "";
//the website to visit is: http://192.168.4.1
WiFiServer server(80);
String html ="<!DOCTYPE html> \
<html> \
<body> \
<center><h1>Distance Alarm Remote Control</h1></center> \
<center><h2>ESP32S2 Web Server Access Point</h2></center> \
<form> \
<button name=\"NOISE\" button style=\"color:green\" value=\"ON\" type=\"submit\">NOISE ON</button> \
<button name=\"NOISE\" button style=\"color=red\" value=\"OFF\" type=\"submit\">NOISE OFF</button><br><br> \
<button name=\"THRESHOLD\" button style=\"color:green\" value=\"UP\" type=\"submit\">THRESHOLD UP</button> \
<button name=\"THRESHOLD\" button style=\"color:red\" value=\"DOWN\" type=\"submit\">THRESHOLD DOWN</button> \
</form> \
</body> \
</html>";
//touchPin: lecture 21
//screen: lecture 21
long duration;  // variable for the duration of sound wave travel
int distance;   // variable for the distance measurement
bool noise = true;
String output[20] = {"","","","","","","","","","","","","","","","","","","",""};


bool alternator = false;  // variable for the alarmLights method
const int alarmButton = 0;
const int UpButton = 16;   // GP Pin 16
const int DownButton = 15;   // GP Pin 16
const int speedOfSound = 0.034;
int threshold = 5;  //in centimeters


const int buzzer = 19;  // GP Pin 3


void setup() {
  pinMode(alarmButton, INPUT_PULLUP);
  pinMode(UpButton, INPUT_PULLUP);
  pinMode(DownButton, INPUT_PULLUP);


  pinMode(led1, OUTPUT);
  pinMode(led2, OUTPUT);
  pinMode(led3, OUTPUT);
  pinMode(led4, OUTPUT);
  pinMode(led5, OUTPUT);
  pinMode(led6, OUTPUT);
  pinMode(led7, OUTPUT);
  pinMode(led8, OUTPUT);
  pinMode(led9, OUTPUT);
  pinMode(led10, OUTPUT);


  pinMode(buzzer, OUTPUT);
  pinMode(redLight, OUTPUT);
  pinMode(blueLight, OUTPUT);
  pinMode(LED_BUILTIN, OUTPUT);


  setupDisplay();
  setupServer();
  //given code
  pinMode(trigPin, OUTPUT);
  pinMode(echoPin, INPUT);


  delay(100);
}
void clearScreen(){
  display.fillScreen(BLACK);
  display.setCursor(0, 1);
}
void displayPrint(String newline){
  shiftLines();
  output[0] = newline;
  printOutput();
}
void shiftLines(){
  for (int i = 19; i > 0; i--){//iterates through every index but the last
    output[i] = output[i - 1];
  }
  output[0] = "";
}
void printOutput(){
  clearScreen();
  for (String line: output){
    display.println(line);
  }
  Serial.println(output[0]);
}
int getNumOfLights(){
  return getNumOfLights(0.3);
}


int getNumOfLights(double ratio){// algorithm determines how many thresholds away the user is
double interval = threshold * ratio;
  if(buttonIsPressed()){
    return 10;
  } else {
    return (10 - ((distance - threshold) / interval)); //the closer to threshold, the more lights
  }
}
void changeThreshold(bool direction){
  if (direction == false) {// if direction is downward
    if (threshold <= 10) {
      threshold -= 10;
      String output = "Threshold down to ";
      output += threshold;
      output += "cm";
      displayPrint(output);
      flash(threshold / 10);
    }
  }
  if (direction == true) {// if direction is upward
    threshold += 10;
    String output = "Threshold up to ";
    output += threshold;
    output += "cm";
    displayPrint(output);
    flash(threshold / 10);
  }
}
void flash(int iterations){
  for (int i = 0; i < iterations ; i++) {
    digitalWrite(BUILTIN_LED, HIGH);
    delay(100);
    digitalWrite(BUILTIN_LED, LOW);
    delay(100);
  }
}


void triggerAlarm() {
  triggerAlarm(false);
}
//prints the message right after distance is printed
void triggerAlarm(bool trigger) {
  String output = "Distance: ";
  output += String(distance);
  output += "cm";
  if (trigger == true) {
    display.setTextColor(RED);
    output += " >:(";
    displayPrint(output);
  } else {
    if (getNumOfLights() > 6) {
      output += " :|";
      display.setTextColor(YELLOW);
    } else {
    output += " :)";
      display.setTextColor(GREEN);
    }
    displayPrint(output);
  }
  Serial.print(output[0]);
  display.print(output[0]);
  alarmLights(trigger);
}
// illuminates two lights in an alternating fashion. Buzzer included as well.
void alarmLights(bool trigger) {
  if (trigger == true) {
    if (alternator == false) {
      if (noise) {
        digitalWrite(buzzer, HIGH);  //buzzer on
      }
      digitalWrite(redLight, LOW);   //red off
      digitalWrite(blueLight, HIGH); //blue on
      alternator = true;
    } else {
      if (noise) {
        digitalWrite(buzzer, HIGH);  //buzzer on
      }
      digitalWrite(blueLight, LOW);  //blue off
      digitalWrite(redLight, HIGH);  //red on
      alternator = false;
    }
  } else {                         //if alarm not triggered
    digitalWrite(buzzer, LOW);     // turn buzzer off
    digitalWrite(blueLight, LOW);  //blue off
    digitalWrite(redLight, LOW);   //red off
  }
}


void clearTheLights(){
  digitalWrite(led1, LOW);  //led off
  digitalWrite(led2, LOW);  //led off
  digitalWrite(led3, LOW);  //led off
  digitalWrite(led4, LOW);  //led off
  digitalWrite(led5, LOW);  //led off
  digitalWrite(led6, LOW);  //led off
  digitalWrite(led7, LOW);  //led off
  digitalWrite(led8, LOW);  //led off
  digitalWrite(led9, LOW);  //led off
  digitalWrite(led10, LOW);  //led off
}


void setupDisplay(){
  display.begin();
  display.fillScreen(BLACK);
  display.setCursor(0, 1);
  display.setTextSize(2);
  display.setTextColor(WHITE);
  display.println("Display Initialized");
}
void setupServer(){
  Serial.begin(115200);
  displayPrint("Setting A.P...");
  // You can remove the password parameter if you want the AP to be open.
  // a valid password must have more than 7 characters
  if (!WiFi.softAP(ssid, password)) {
    log_e("Soft AP creation failed.");
    while (1)
      ;
  }
  IPAddress myIP = WiFi.softAPIP();
  //This part cannot be obfuscated through displayPrint, so don't try.
  Serial.print("AP IP address: ");
  Serial.println(myIP);
  Serial.println("Server started");
  display.print("AP IP address: ");
  display.println(myIP);
  display.println("Server started");
  server.begin();
}
void illuminateDistance(int distance){
   illuminateDistance(distance, .3);
}
void illuminateDistance(int distance, double ratio){
  double interval = threshold * ratio;
  int numOfLights;
  if(buttonIsPressed()){
    numOfLights = 10;
  } else {
    numOfLights = 10 - ((distance - threshold) / interval); //the closer to threshold, the more lights
  }
  clearTheLights();
  if(numOfLights > 0){
    digitalWrite(led1, HIGH);  //led on
  }
  if(numOfLights > 1){
    digitalWrite(led2, HIGH);  //led on
  }
  if(numOfLights > 2){
    digitalWrite(led3, HIGH);  //led on
  }
  if(numOfLights > 3){
    digitalWrite(led4, HIGH);  //led on
  }
  if(numOfLights > 4){
    digitalWrite(led5, HIGH);  //led on
  }
  if(numOfLights > 5){
    digitalWrite(led6, HIGH);  //led on
  }
  if(numOfLights > 6){
    digitalWrite(led7, HIGH);  //led on
  }
  if(numOfLights > 7){
    digitalWrite(led8, HIGH);  //led on
  }
  if(numOfLights > 8){
    digitalWrite(led9, HIGH);  //led on
  }
  if(numOfLights > 9){
    digitalWrite(led10, HIGH);  //led on
  }
}
bool buttonIsPressed() {
  int buttonVal = digitalRead(alarmButton);  //param = button GP pin
  if (buttonVal == LOW) {                    //if button is pressed
    return true;
  } else {
    return false;
  }
}


void loop() {
  // Clears the trigPin condition
  digitalWrite(trigPin, LOW);
  delayMicroseconds(2);


  // Sets the trigPin HIGH (ACTIVE) for 10 microseconds. Given code.
  digitalWrite(trigPin, HIGH);
  delayMicroseconds(10);
  digitalWrite(trigPin, LOW);


  // Reads the echoPin, returns the sound wave travel time in microseconds
  duration = pulseIn(echoPin, HIGH);
  distance = duration * 0.034 / 2;  // Calculating the distance
  clearScreen();
  illuminateDistance(distance);
  triggerAlarm((distance <= threshold) || buttonIsPressed());


  //-- WiFi management --//
  WiFiClient client = server.available();  // listen for incoming clients


  if (client) {// if you get a client,
    String request = client.readStringUntil('\r');
    if(request.indexOf("NOISE=ON") != -1) noise = true;
    if(request.indexOf("NOISE=OFF") != -1) noise = false;
    if(request.indexOf("THRESHOLD=UP") != -1) changeThreshold(true);
    if(request.indexOf("THRESHOLD=DOWN") != -1) changeThreshold(false);            
    client.print(html);
    client.stop();
    displayPrint("Client Disconnected.");
  }
  delay(250);
}
